# Fritzing sketch main (saved by Fritzing 0.9.4)

parts:
  SW1 = Rotary_encoder [package=encoder_led_3]
  SW2 = Rotary_encoder [package=encoder_led_3]
  SW3 = Rotary_encoder [package=encoder_led_3]
  U4 = Slide_potentiometer_10k [package=slider]
  U5 = Slide_potentiometer_10k [package=slider]
  U6 = Slide_potentiometer_10k [package=slider]
  Pro_Micro1 = SparkFun Pro Micro
  S1 = Round Pushbutton
  S2 = Round Pushbutton
  S3 = Round Pushbutton
  S4 = Round Pushbutton
  S5 = Round Pushbutton
  S6 = Round Pushbutton
  S7 = Round Pushbutton
  S8 = Round Pushbutton
  S9 = Round Pushbutton
  S10 = Round Pushbutton
  S11 = Round Pushbutton
  S12 = Round Pushbutton
  S13 = Round Pushbutton
  S14 = Round Pushbutton
  S15 = Round Pushbutton
  S16 = Round Pushbutton
  Part1 = Analog Digital MUX Breakout
  IC2 = MC14490P [package="DIP16 [THT]"]
  C1 = Capacitor [package=cap-pth-small2]
  IC3 = MC14490P [package="DIP16 [THT]"]
  C2 = Capacitor [package=cap-pth-small2]
  C3 = Capacitor [package=cap-pth-small2]
  IC4 = MC14490P [package="DIP16 [THT]"]

nets:
  N1: SW1.CLK, Pro_Micro1.RX1
  N2: SW1.DT, Pro_Micro1.7
  N3: SW1.SW, Pro_Micro1.9
  VCC: SW1.+, SW2.+, SW3.+, U4.VCC, U5.VCC, U6.VCC, Pro_Micro1.VCC, Part1.VCC, IC3.VDD, IC4.VDD
  GND: SW1.GND, SW2.GND, SW3.GND, U4.GND, U5.GND, U6.GND, Pro_Micro1.GND, S1.leg1, Part1.GND, Part1.EN, IC3.Vss, IC4.Vss
  N4: SW2.CLK, Pro_Micro1.8
  N5: SW2.DT, Pro_Micro1.TX0
  N6: SW2.SW, Pro_Micro1.5
  N7: SW3.CLK, Pro_Micro1.3
  N8: SW3.DT, Pro_Micro1.2
  N9: SW3.SW, Pro_Micro1.6
  N10: U4.OTB, Pro_Micro1.A0
  N11: U5.OTB, Pro_Micro1.A1
  N12: U6.OTB, Pro_Micro1.A2
  N13: Pro_Micro1.10, Part1.S0
  N14: Pro_Micro1.16, Part1.S1
  N15: Pro_Micro1.14, Part1.S2
  N16: Pro_Micro1.15, Part1.S3
  N17: Pro_Micro1.A3, Part1.SIG
  N18: S1.leg0, IC2.Aout
  N19: S2.leg0, IC2.Bout
  N20: S3.leg0, IC2.Cout
  N21: S4.leg0, IC2.Eout
  N22: S5.leg0, IC2.Fout
  N23: S6.leg0, IC3.Aout
  N24: S7.leg0, IC2.Dout
  N25: S8.leg0, IC3.Bout
  N26: S9.leg0, IC3.Cout
  N27: S10.leg0, IC3.Fout
  N28: S11.leg0, IC3.Eout
  N29: S12.leg0, IC3.Dout
  N30: S13.leg0, IC4.Aout
  N31: S14.leg0, IC4.Dout
  N32: S15.leg0, IC4.Cout
  N33: S16.leg0, IC4.Bout
  N34: Part1.C0, IC2.Ain
  N35: Part1.C1, IC2.Bin
  N36: Part1.C2, IC2.Cin
  N37: Part1.C3, IC2.Din
  N38: Part1.C4, IC2.Ein
  N39: Part1.C5, IC2.Fin
  N40: Part1.C6, IC3.Ain
  N41: Part1.C7, IC3.Bin
  N42: Part1.C8, IC3.Cin
  N43: Part1.C9, IC3.Din
  N44: Part1.C10, IC3.Fin
  N45: Part1.C11, IC3.Ein
  N46: Part1.C12, IC4.Ain
  N47: Part1.C13, IC4.Bin
  N48: Part1.C14, IC4.Cin
  N49: Part1.C15, IC4.Din
  N50: IC2.OSCin, C1.2
  N51: IC2.OSCout, C1.1
  N52: IC3.OSCin, C2.2
  N53: IC3.OSCout, C2.1
  N54: C3.1, IC4.OSCout
  N55: C3.2, IC4.OSCin

notes:
  Interrupt pin 7 & 0
  Interrupt
  Interrupt pin 1
  pin 2 & 3

custom parts:
  Rotary_encoder: 360 Degrees Rotary Encoder Module For Arduino
  Slide_potentiometer_10k: Slide Potentiometer 10K Linear Module Dual Output for Arduino AVR Electronic Block
  SparkFun Pro Micro: The Pro Micro is similar to the Pro Mini except with an ATmega32U4 on board. The USB transceiver inside the 32U4 allows us to add USB connectivity on-board and do away with bulky external USB interface. Based on: https://github.com/unorthodox-engineers/unorthodox-arduino/blob/master/Unorthodox/fritzing/parts/Pro%20Micro.fzpz
  MC14490P: MC14490P DIP-16 MC14490 DIP16 MC14490PG DIP logic chip hardware debouncer
