# Fritzing sketch main_with_module (saved by Fritzing 0.9.4)

parts:
  U7 = Slide_potentiometer_10k [package=slider]  # not connected
  U8 = Slide_potentiometer_10k [package=slider]  # not connected
  U9 = Slide_potentiometer_10k [package=slider]  # not connected
  Pro_Micro2 = SparkFun Pro Micro
  SW2 = Rotary_encoder [package=encoder_led_3]  # not connected
  SW3 = Rotary_encoder [package=encoder_led_3]  # not connected
  SW5 = Rotary_encoder [package=encoder_led_3]  # not connected
  Pro_Micro4 = SparkFun Pro Micro  # not connected
  Part2 = Analog Digital MUX Breakout  # not connected
  S17 = Round Pushbutton  # not connected
  S18 = Round Pushbutton  # not connected
  S19 = Round Pushbutton  # not connected
  S20 = Round Pushbutton  # not connected
  S21 = Round Pushbutton  # not connected
  S22 = Round Pushbutton  # not connected
  S23 = Round Pushbutton  # not connected
  S24 = Round Pushbutton  # not connected
  S25 = Round Pushbutton  # not connected
  S26 = Round Pushbutton  # not connected
  S27 = Round Pushbutton  # not connected
  S28 = Round Pushbutton  # not connected
  S29 = Round Pushbutton  # not connected
  S30 = Round Pushbutton  # not connected
  S31 = Round Pushbutton  # not connected
  S32 = Round Pushbutton  # not connected

nets:
  N1: Pro_Micro2.3, Pro_Micro2.4

notes:
  +5V
  A0 (18)
  A1 (19)
  A2 (20)
  Pot1
  Pot2
  Pot3
  TX0(1)
  RX1(0)
  9
  2
  3
  8
  Enc1
  Enc2
  KEY1
  KEY2
  clk Enc1
  clk Enc2
  dt  Enc2
  5
  6
  KEY3
  Main Arduino
  Enc Controller
  Enc3
  left enc controller
  dt Enc1
  KEY3C
  right enc controller
  clk Enc3
  dt Enc3
  7
  10
  16
  14
  15
  21
  Multiplexer
  S0
  S1
  S2
  S3
  SIG
  B1
  B2
  B3
  B4
  B7
  B6
  B5
  B8
  B15
  B13
  B14
  B11
  B12
  B16
  B10
  B9
  Button Pad
  C0
  C4
  C12
  C8
  C9
  C13
  C5
  C1
  C10
  C14
  C6
  C2
  C11
  C15
  C7
  C3
  Hardware
  Arduino IDE
  TX0
  1
  RX1
  0
  A0
  A1
  A2
  A3
  18
  19
  20

custom parts:
  Slide_potentiometer_10k: Slide Potentiometer 10K Linear Module Dual Output for Arduino AVR Electronic Block
  SparkFun Pro Micro: The Pro Micro is similar to the Pro Mini except with an ATmega32U4 on board. The USB transceiver inside the 32U4 allows us to add USB connectivity on-board and do away with bulky external USB interface. Based on: https://github.com/unorthodox-engineers/unorthodox-arduino/blob/master/Unorthodox/fritzing/parts/Pro%20Micro.fzpz
  Rotary_encoder: 360 Degrees Rotary Encoder Module For Arduino
